// Digital circuit accumulator.dig as structural Verilog
module accumulator (
  input  [7:0] D,
  input  Clock,
  input  Enable,
  output [7:0] Q
);

  register_8bit register_8bit_1 (.D(D), .Clock(Clock), .Enable(Enable), .Q(Q));
endmodule
