// Digital circuit adder-8bit.dig as structural Verilog
module adder_8bit (
  input  [7:0] A,
  input  [7:0] B,
  input  Ci,
  output [7:0] Sum,
  output Co
);

  wire C0, C1, C2, C3, C4, C5, C6;

  full_adder full_adder_1 (.A(A[0]), .B(B[0]), .Ci(Ci), .Sum(Sum[0]), .Co(C0));
  full_adder full_adder_2 (.A(A[1]), .B(B[1]), .Ci(C0), .Sum(Sum[1]), .Co(C1));
  full_adder full_adder_3 (.A(A[2]), .B(B[2]), .Ci(C1), .Sum(Sum[2]), .Co(C2));
  full_adder full_adder_4 (.A(A[3]), .B(B[3]), .Ci(C2), .Sum(Sum[3]), .Co(C3));
  full_adder full_adder_5 (.A(A[4]), .B(B[4]), .Ci(C3), .Sum(Sum[4]), .Co(C4));
  full_adder full_adder_6 (.A(A[5]), .B(B[5]), .Ci(C4), .Sum(Sum[5]), .Co(C5));
  full_adder full_adder_7 (.A(A[6]), .B(B[6]), .Ci(C5), .Sum(Sum[6]), .Co(C6));
  full_adder full_adder_8 (.A(A[7]), .B(B[7]), .Ci(C6), .Sum(Sum[7]), .Co(Co));

  // Other names for the same wires on the sheet: C7 = Co; S0 = Sum[0]; S1 = Sum[1]; S2 = Sum[2]; S3 = Sum[3];
  //   S4 = Sum[4]; S5 = Sum[5]; S6 = Sum[6]; S7 = Sum[7]
endmodule
