// Digital circuit alu-8bit.dig as structural Verilog
module alu_8bit (
  input  [7:0] A,
  input  [7:0] B,
  input  [2:0] Opcode,
  output [7:0] Result
);

  wire [7:0] ADD, DEC, DIV, INC, MUL, SUB;

  adder_8bit adder_8bit_1 (.A(A), .B(B), .Ci(1'b0), .Sum(ADD));  // open: Co
  subtractor_8bit subtractor_8bit_1 (.A(A), .B(B), .Diff(SUB));
  incrementor_8bit incrementor_8bit_1 (.A(A), .Result(INC));
  decrementor_8bit decrementor_8bit_1 (.A(A), .Result(DEC));
  multiplier_4x4 multiplier_4x4_1 (.A(A[3:0]), .B(B[3:0]), .Product(MUL));
  divisor_4x4 divisor_4x4_1 (.A(A[3:0]), .B(B[3:0]), .Q(DIV[3:0]), .R(DIV[7:4]));
  Multiplexer #(.Selector_Bits(3), .Bits(8)) multiplexer_1 (
    .sel(Opcode), .in_0(ADD), .in_1(SUB), .in_2(INC), .in_3(DEC), .in_4(MUL), .in_5(DIV), .in_6(8'h1),
    .in_7(8'h1), .out(Result));

  // Other names for the same wires on the sheet: A_lo[3:0] = A[3:0]; B_lo[3:0] = B[3:0]
endmodule
