// Digital circuit decrementor-8bit.dig as structural Verilog
module decrementor_8bit (
  input  [7:0] A,
  output [7:0] Result
);

  adder_8bit adder_8bit_1 (.A(A), .B({8{1'b1}}), .Ci(1'b0), .Sum(Result));  // open: Co
endmodule
