// Digital circuit divide-step.dig as structural Verilog
module divide_step (
  input  [3:0] R_in,
  input  A_in,
  input  [3:0] B_in,
  output [3:0] R_out,
  output Q_out
);

  wire Sign;
  wire [3:0] Sub_lower4;

  subtractor_5bit subtractor_5bit_1 (.A({R_in, A_in}), .B({1'b0, B_in}), .Diff({Sign, Sub_lower4}));
  Multiplexer #(.Bits(4)) multiplexer_1 (.sel(Sign), .in_0(Sub_lower4), .in_1({R_in[2:0], A_in}), .out(R_out));
  not not_1 (Q_out, Sign);

  // Other names for the same wires on the sheet: Shifted[4:0] = {R_in, A_in}; Shifted_lower4[3:0] = {R_in[2:0], A_in};
  //   B_ext[3:0] = B_in; Shifted_MSB = R_in[3]; Sub_result[4:0] = {Sign, Sub_lower4}
endmodule
