// Digital circuit divisor-4x4.dig as structural Verilog
module divisor_4x4 (
  input  [3:0] A,
  input  [3:0] B,
  output [3:0] Q,
  output [3:0] R
);

  wire divide_step_2_p1, divide_step_2_p3, divide_step_2_p5, divide_step_2_p10, divide_step_2_p11,
       divide_step_2_p17, divide_step_2_p19, divide_step_4_p1, divide_step_4_p5, divide_step_4_p6, R3;
  wire [3:0] R1, R2;

  divide_step divide_step_1 (.R_in(4'b0000), .A_in(A[3]), .B_in(B), .R_out(R1), .Q_out(Q[3]));
  // divide_step divide_step_2: pin names not known; wires that end beside it: divide_step_2_p1, R2, divide_step_2_p3, A[1], divide_step_2_p5, B, divide_step_2_p1, divide_step_2_p3, divide_step_2_p5, divide_step_2_p10, divide_step_2_p11, divide_step_2_p10, R3, divide_step_2_p11, Q[1], R3, divide_step_2_p17, A[0], divide_step_2_p19, B
  divide_step divide_step_3 (.R_in(R1), .A_in(A[2]), .B_in(B), .R_out(R2), .Q_out(Q[2]));
  // divide_step divide_step_4: pin names not known; wires that end beside it: divide_step_4_p1, divide_step_4_p1, divide_step_2_p17, divide_step_2_p19, divide_step_4_p5, divide_step_4_p6, divide_step_4_p5, R, divide_step_4_p6, Q[0]

  // Other names for the same wires on the sheet: R_final[3:0] = R
endmodule
