// Digital circuit full-adder.dig as structural Verilog
module full_adder (
  input  A,
  input  B,
  input  Ci,
  output Sum,
  output Co
);

  wire Carry1, Carry2, Sum1;

  half_adder half_adder_1 (.A(A), .B(B), .Sum(Sum1), .Carry(Carry1));
  half_adder half_adder_2 (.A(Sum1), .B(Ci), .Sum(Sum), .Carry(Carry2));
  or or_1 (Co, Carry1, Carry2);
endmodule
