// Digital circuit incrementor-8bit.dig as structural Verilog
module incrementor_8bit (
  input  [7:0] A,
  output [7:0] Result
);

  adder_8bit adder_8bit_1 (.A(A), .B(8'h1), .Ci(1'b0), .Sum(Result));  // open: Co
endmodule
