// Digital circuit multiplier-4x4.dig as structural Verilog
module multiplier_4x4 (
  input  [3:0] A,
  input  [3:0] B,
  output [7:0] Product
);

  wire P00, P01, P02, P03, P10, P11, P12, P13, P20, P21, P22, P23, P30, P31, P32, P33;
  wire [7:0] Sum01, Sum012;

  and and_1 (P00, A[0], B[0]);
  and and_2 (P01, A[0], B[1]);
  and and_3 (P02, A[0], B[2]);
  and and_4 (P03, A[0], B[3]);
  adder_8bit adder_8bit_1 (
    .A({4'b0000, P30, P20, P10, P00}), .B({3'b000, P31, P21, P11, P01, 1'b0}), .Ci(1'b0), .Sum(Sum01));  // open: Co
  and and_5 (P10, A[1], B[0]);
  and and_6 (P11, A[1], B[1]);
  and and_7 (P12, A[1], B[2]);
  and and_8 (P13, A[1], B[3]);
  adder_8bit adder_8bit_2 (.A(Sum01), .B({2'b00, P32, P22, P12, P02, 2'b00}), .Ci(1'b0), .Sum(Sum012));  // open: Co
  and and_9 (P20, A[2], B[0]);
  and and_10 (P21, A[2], B[1]);
  and and_11 (P22, A[2], B[2]);
  and and_12 (P23, A[2], B[2]);
  and and_13 (P30, A[3], B[0]);
  and and_14 (P31, A[3], B[1]);
  and and_15 (P32, A[3], B[2]);
  and and_16 (P33, A[3], B[3]);
  adder_8bit adder_8bit_3 (.A(Sum012), .B({1'b0, P33, P23, P13, P03, 3'b000}), .Ci(1'b0), .Sum(Product));  // open: Co

  // Other names for the same wires on the sheet: Row0[3:0] = {P30, P20, P10, P00}; Row1[4:1] = {P31, P21, P11, P01};
  //   Row2[5:2] = {P32, P22, P12, P02}; Row3[6:3] = {P33, P23, P13, P03}
endmodule
