// Digital circuit pc.dig as structural Verilog
module pc (
  input  Clock,
  input  Reset,
  input  Enable,
  input  Load,
  input  [7:0] LoadAddr,
  output [7:0] PC
);

  wire [7:0] MUX1_Out, MUX2_Out, PC_Inc, REG_D;

  incrementor_8bit incrementor_8bit_1 (.A(PC), .Result(PC_Inc));
  Multiplexer #(.Bits(8)) multiplexer_1 (.sel(Load), .in_0(MUX1_Out), .in_1(LoadAddr), .out(MUX2_Out));
  Multiplexer #(.Bits(8)) multiplexer_2 (.sel(Reset), .in_0(MUX2_Out), .in_1({8{1'b0}}), .out(REG_D));
  Multiplexer #(.Bits(8)) multiplexer_3 (.sel(Enable), .in_0(PC), .in_1(PC_Inc), .out(MUX1_Out));
  register_8bit register_8bit_1 (.D(REG_D), .Clock(Clock), .Enable(1'b1), .Q(PC));

  // Other names for the same wires on the sheet: PC_Q[7:0] = PC
endmodule
