// Digital circuit register-8bit.dig as structural Verilog
module register_8bit (
  input  [7:0] D,
  input  Clock,
  input  Enable,
  output [7:0] Q
);

  wire multiplexer_1_out, multiplexer_2_out, multiplexer_3_out, multiplexer_4_out, multiplexer_5_out,
       multiplexer_6_out, multiplexer_7_out, multiplexer_8_out;

  Multiplexer #(.Bits(1)) multiplexer_1 (.sel(Enable), .in_0(Q[0]), .in_1(D[0]), .out(multiplexer_1_out));
  Multiplexer #(.Bits(1)) multiplexer_2 (.sel(Enable), .in_0(Q[1]), .in_1(D[1]), .out(multiplexer_2_out));
  Multiplexer #(.Bits(1)) multiplexer_3 (.sel(Enable), .in_0(Q[2]), .in_1(D[2]), .out(multiplexer_3_out));
  Multiplexer #(.Bits(1)) multiplexer_4 (.sel(Enable), .in_0(Q[3]), .in_1(D[3]), .out(multiplexer_4_out));
  Multiplexer #(.Bits(1)) multiplexer_5 (.sel(Enable), .in_0(Q[4]), .in_1(D[4]), .out(multiplexer_5_out));
  Multiplexer #(.Bits(1)) multiplexer_6 (.sel(Enable), .in_0(Q[5]), .in_1(D[5]), .out(multiplexer_6_out));
  Multiplexer #(.Bits(1)) multiplexer_7 (.sel(Enable), .in_0(Q[6]), .in_1(D[6]), .out(multiplexer_7_out));
  Multiplexer #(.Bits(1)) multiplexer_8 (.sel(Enable), .in_0(Q[7]), .in_1(D[7]), .out(multiplexer_8_out));
  D_FF d_ff_1 (.D(multiplexer_1_out), .C(Clock), .Q(Q[0]));  // open: nQ
  D_FF d_ff_2 (.D(multiplexer_2_out), .C(Clock), .Q(Q[1]));  // open: nQ
  D_FF d_ff_3 (.D(multiplexer_3_out), .C(Clock), .Q(Q[2]));  // open: nQ
  D_FF d_ff_4 (.D(multiplexer_4_out), .C(Clock), .Q(Q[3]));  // open: nQ
  D_FF d_ff_5 (.D(multiplexer_5_out), .C(Clock), .Q(Q[4]));  // open: nQ
  D_FF d_ff_6 (.D(multiplexer_6_out), .C(Clock), .Q(Q[5]));  // open: nQ
  D_FF d_ff_7 (.D(multiplexer_7_out), .C(Clock), .Q(Q[6]));  // open: nQ
  D_FF d_ff_8 (.D(multiplexer_8_out), .C(Clock), .Q(Q[7]));  // open: nQ
endmodule
