// Digital circuit subtractor-5bit.dig as structural Verilog
module subtractor_5bit (
  input  [4:0] A,
  input  [4:0] B,
  output [4:0] Diff
);

  wire [4:0] B_inv;

  assign B_inv = ~B;  // Not not_1, 5 bits wide
  adder_5bit adder_5bit_1 (.A(A), .B(B_inv), .Ci(1'b1), .Sum(Diff));  // open: Co
endmodule
