// Digital circuit subtractor-8bit.dig as structural Verilog
module subtractor_8bit (
  input  [7:0] A,
  input  [7:0] B,
  output [7:0] Diff
);

  wire [7:0] B_inv;

  assign B_inv = ~B;  // Not not_1, 8 bits wide
  adder_8bit adder_8bit_1 (.A(A), .B(B_inv), .Ci(1'b1), .Sum(Diff));  // open: Co
endmodule
