// Digital circuit zero-comparator.dig as structural Verilog
module zero_comparator (
  input  [7:0] A,
  output IsZero
);

  Comparator #(.Bits(8)) comparator_1 (.a(A), .b({8{1'b0}}), .eq(IsZero));  // open: gt, lt
endmodule
